# Fritzing sketch scarp (saved by Fritzing 1.0.2b)
circuit board: 9cm x 9cm
breadboards: 2

parts:
  R1 = Resistor [tolerance=±5% power=0.25 resistance=1k package=THT]
  J4 = female pin header, 20 pins [form="♀ (female)"]
  Raspberry_Pi_Pico = Raspberry Pi Pico
  R9 = Rotary Potentiometer (Small) [maximum_resistance=10kΩ knob_status=50% power=0.5W package=THT]
  R10 = Rotary Potentiometer (Small) [maximum_resistance=10kΩ knob_status=50% power=0.5W package=THT]
  LED1 = LED - 3mm [color="Red (633nm)" current=0.030A package="3 mm [THT]"]
  R2 = Resistor [tolerance=±5% power=0.25 resistance=1k package=THT]
  LED2 = LED - 3mm [color="Red (633nm)" current=0.030A package="3 mm [THT]"]
  R3 = Resistor [tolerance=±5% power=0.25 resistance=1k package=THT]
  LED3 = LED - 3mm [color="Red (633nm)" current=0.030A package="3 mm [THT]"]
  R4 = Resistor [tolerance=±5% power=0.25 resistance=1k package=THT]
  LED4 = LED - 3mm [color="Red (633nm)" current=0.030A package="3 mm [THT]"]
  R5 = Resistor [tolerance=±5% power=0.25 resistance=1k package=THT]
  LED5 = LED - 3mm [color="Red (633nm)" current=0.030A package="3 mm [THT]"]
  R6 = Resistor [tolerance=±5% power=0.25 resistance=1k package=THT]
  LED6 = LED - 3mm [color="Red (633nm)" current=0.030A package="3 mm [THT]"]
  R7 = Resistor [tolerance=±5% power=0.25 resistance=1k package=THT]
  LED7 = LED - 3mm [color="Red (633nm)" current=0.030A package="3 mm [THT]"]
  R8 = Resistor [tolerance=±5% power=0.25 resistance=1k package=THT]
  LED8 = LED - 3mm [color="Red (633nm)" current=0.030A package="3 mm [THT]"]
  V1 = DC Power [voltage=5]
  S1 = Pushbutton [package="[THT]"]
  S2 = Pushbutton [package="[THT]"]
  S3 = Pushbutton [package="[THT]"]
  S4 = Pushbutton [package="[THT]"]
  S5 = Pushbutton [package="[THT]"]
  S6 = Pushbutton [package="[THT]"]
  S7 = Pushbutton [package="[THT]"]
  S8 = Pushbutton [package="[THT]"]
  oled = OLED 0.96" 128x64 I2C SSD1306
  Audio = Audio Jack (TRS) 3.5mm [package="PG203J [THT]"]
  MidiIn = Audio Jack (TRS) 3.5mm [package="PG203J [THT]"]
  MidiOut = Audio Jack (TRS) 3.5mm [package="PG203J [THT]"]
  6N137 = IC, DIP package, 8 pins [chip_label=IC]
  C1 = Capacitor [package=cap-pth-5mm]
  V2 = DC Power [voltage=5]  # not connected
  R13 = Resistor [tolerance=±5% resistance=33 power=0.25W package=THT]
  R12 = Resistor [tolerance=±5% resistance=220 power=0.25W package=THT]
  R11 = Resistor [tolerance=±5% resistance=4.7k power=0.25W package=THT]
  R15 = Resistor [tolerance=±5% resistance=10 power=0.25W package=THT]
  D2 = Rectifier Diode [part_number=1N4001 package="300 mil [THT]"]
  RE2 = Rotary Encoder Pushbutton [mn=EC12E20-24P24C-SW mpn=SRPassives package=THT]
  J2 = female pin header, 20 pins [form="♀ (female)"]

nets:
  N1: R1.Pin_0, LED1.cathode
  GND: R1.Pin_1, J4.pin3, J4.pin8, J4.pin13, J4.pin18, Raspberry_Pi_Pico.pin_3, Raspberry_Pi_Pico.pin_8, Raspberry_Pi_Pico.pin_13, Raspberry_Pi_Pico.pin_18, Raspberry_Pi_Pico.pin_23, Raspberry_Pi_Pico.pin_28, Raspberry_Pi_Pico.pin_33, Raspberry_Pi_Pico.pin_38, R9.leg2, R10.leg2, R2.Pin_1, R3.Pin_1, R4.Pin_1, R5.Pin_1, R6.Pin_1, R7.Pin_1, R8.Pin_1, S1.Pin_3, S1.Pin_4, S2.Pin_3, S2.Pin_4, S3.Pin_3, S3.Pin_4, S4.Pin_3, S4.Pin_4, S5.Pin_3, S5.Pin_4, S6.Pin_3, S6.Pin_4, S7.Pin_3, S7.Pin_4, S8.Pin_3, S8.Pin_4, oled.GND, Audio.Sleeve, MidiIn.Sleeve, MidiOut.Sleeve, 6N137.pin5, C1.1, RE2.SwitchPin2, RE2.GND_Pin1, J2.pin3, J2.pin8, J2.pin13, J2.pin18
  N2: J4.pin1, Raspberry_Pi_Pico.pin_40, V1.V-
  N3: J4.pin2, Raspberry_Pi_Pico.pin_39
  N4: J4.pin4, Raspberry_Pi_Pico.pin_37
  N5: J4.pin5, Raspberry_Pi_Pico.pin_36, oled.VCC, 6N137.pin8, C1.2, R13.Pin_1, R11.Pin_0
  N6: J4.pin6, Raspberry_Pi_Pico.pin_35
  N7: J4.pin7, Raspberry_Pi_Pico.pin_34, RE2.SwitchPin1
  N8: J4.pin9, Raspberry_Pi_Pico.pin_32, R9.wiper
  N9: J4.pin10, Raspberry_Pi_Pico.pin_31, R10.wiper
  N10: J4.pin11, Raspberry_Pi_Pico.pin_30, RE2.EncoderPinC
  N11: J4.pin12, Raspberry_Pi_Pico.pin_29, Audio.Ring, Audio.Tip
  N12: J4.pin14, Raspberry_Pi_Pico.pin_27, oled.SCL
  N13: J4.pin15, Raspberry_Pi_Pico.pin_26, oled.SCA
  N14: J4.pin16, Raspberry_Pi_Pico.pin_25, RE2.EncoderPinB
  N15: J4.pin17, Raspberry_Pi_Pico.pin_24, RE2.EncoderPinA
  N16: J4.pin19, Raspberry_Pi_Pico.pin_22, 6N137.pin6, R11.Pin_1
  N17: J4.pin20, Raspberry_Pi_Pico.pin_21, R15.Pin_0
  N18: Raspberry_Pi_Pico.pin_1, S1.Pin_1, S1.Pin_2, J2.pin1
  N19: Raspberry_Pi_Pico.pin_2, LED1.anode, J2.pin2
  N20: Raspberry_Pi_Pico.pin_4, S2.Pin_1, S2.Pin_2, J2.pin4
  N21: Raspberry_Pi_Pico.pin_5, LED2.anode, J2.pin5
  N22: Raspberry_Pi_Pico.pin_6, S3.Pin_1, S3.Pin_2, J2.pin6
  N23: Raspberry_Pi_Pico.pin_7, LED3.anode, J2.pin7
  N24: Raspberry_Pi_Pico.pin_9, S4.Pin_1, S4.Pin_2, J2.pin9
  N25: Raspberry_Pi_Pico.pin_10, LED4.anode, J2.pin10
  N26: Raspberry_Pi_Pico.pin_11, S5.Pin_1, S5.Pin_2, J2.pin11
  N27: Raspberry_Pi_Pico.pin_12, LED5.anode, J2.pin12
  N28: Raspberry_Pi_Pico.pin_14, S6.Pin_1, S6.Pin_2, J2.pin14
  N29: Raspberry_Pi_Pico.pin_15, LED6.anode, J2.pin15
  N30: Raspberry_Pi_Pico.pin_16, S7.Pin_1, S7.Pin_2, J2.pin16
  N31: Raspberry_Pi_Pico.pin_17, LED7.anode, J2.pin17
  N32: Raspberry_Pi_Pico.pin_19, S8.Pin_1, S8.Pin_2, J2.pin19
  N33: Raspberry_Pi_Pico.pin_20, LED8.anode, J2.pin20
  N34: R9.leg1, R10.leg1
  N35: R2.Pin_0, LED2.cathode
  N36: R3.Pin_0, LED3.cathode
  N37: R4.Pin_0, LED4.cathode
  N38: R5.Pin_0, LED5.cathode
  N39: R6.Pin_0, LED6.cathode
  N40: R7.Pin_0, LED7.cathode
  N41: R8.Pin_0, LED8.cathode
  N42: MidiIn.Ring, R12.Pin_0
  N43: MidiIn.Tip, 6N137.pin3, D2.anode
  N44: MidiOut.Ring, R13.Pin_0
  N45: MidiOut.Tip, R15.Pin_1
  N46: 6N137.pin2, R12.Pin_1, D2.cathode

notes:
  scarp v1.0.0
  Pikorredux (2024-02-06)
  Made with fritzing
  USB
  ! 3,3V from the Pico !
  poetaster.de 2024

custom parts:
  Raspberry Pi Pico: Raspberry Pi Pico. Based around the RP2040 microcontroller the Pico is a low cost microcontroller device bringing Raspberry Pi quality, cost, and easy of use to the microcontroller space. Jan 2021, Split part in to two versions: tht (this one) and SMD. This one will drill holes for a .1 in header in pcb to allow plugging in the module as well as providing pads to solder the module to the top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
  Rotary Encoder Pushbutton: Rotary Encoder with pushbutton from SRPassives part EC12E20-24P24C-SW.

// code stored in the sketch: EasyPicoPCB.ino

